// Digital circuit 2BitZaehler.dig as structural Verilog
module _2BitZaehler (
  input  Clk,
  output o1,
  output o2
);

  D_FF d_ff_1 (.D(o1), .C(Clk), .Q(o2));  // open: nQ
  D_FF d_ff_2 (.D(o2), .C(Clk), .nQ(o1));  // open: Q
endmodule
