// Digital circuit 4bitadder.dig as structural Verilog
module _4bitadder (
  input  a__1er,
  input  a__2er,
  input  b__8er,
  input  b__4er,
  input  b__2er,
  input  b__1er,
  input  a__4er,
  input  a__8er,
  output c__1er,
  output c__2er,
  output c__4er,
  output c__8er,
  output Failsafe
);

  wire adder_1_h, fulladder_1_h, fulladder_2_h;

  adder adder_1 (.a(b__1er), .b(a__1er), .h(adder_1_h), .l(c__1er));
  fulladder fulladder_1 (.a(adder_1_h), .b(b__2er), .c(a__2er), .h(fulladder_1_h), .l(c__2er));
  fulladder fulladder_2 (.a(fulladder_1_h), .b(b__4er), .c(a__4er), .h(fulladder_2_h), .l(c__4er));
  fulladder fulladder_3 (.a(fulladder_2_h), .b(b__8er), .c(a__8er), .h(Failsafe), .l(c__8er));
endmodule
