// Digital circuit ampel.dig as structural Verilog
module ampel (
  input  clk
);

  wire _2bitzaehler_1_o1, _2bitzaehler_1_o2, and_1_out, and_2_out, and_3_out, and_4_out, not_1_out,
       not_2_out, or_1_out;

  _2BitZaehler _2bitzaehler_1 (.Clk(clk), .o1(_2bitzaehler_1_o1), .o2(_2bitzaehler_1_o2));
  not not_1 (not_1_out, _2bitzaehler_1_o1);
  not not_2 (not_2_out, _2bitzaehler_1_o2);
  and and_1 (and_1_out, not_1_out, not_2_out);
  and and_2 (and_2_out, not_1_out, _2bitzaehler_1_o2);
  and and_3 (and_3_out, not_2_out, _2bitzaehler_1_o1);
  and and_4 (and_4_out, _2bitzaehler_1_o2, _2bitzaehler_1_o1);
  or or_1 (or_1_out, and_1_out, and_4_out);
  LED led_1 (.in(not_1_out));
  LED led_2 (.in(or_1_out));
  LED led_3 (.in(and_3_out));
  LED led_4 (.in(_2bitzaehler_1_o1));
  LED led_5 (.in(or_1_out));
  LED led_6 (.in(and_2_out));
  LED led_7 (.in(_2bitzaehler_1_o1));
  LED led_8 (.in(or_1_out));
  LED led_9 (.in(and_2_out));
  LED led_10 (.in(not_1_out));
  LED led_11 (.in(or_1_out));
  LED led_12 (.in(and_3_out));
endmodule
