// Digital circuit arithmeticunit.dig as structural Verilog
module arithmeticunit (
  input  in_5,
  input  in_6,
  input  in_7,
  input  in_8,
  input  in_9,
  input  in_10,
  input  in_11,
  input  in_12,
  input  in_13,
  input  in_14,
  output out_1,
  output out_2,
  output out_3,
  output out_4,
  output out_15
);

  wire _4bitadder_1_c__1er, _4bitadder_1_c__2er, _4bitadder_1_c__4er, _4bitadder_1_c__8er,
       _4bitadder_1_failsafe, not_1_out, selector_5_c, selector_6_c, selector_7_c, selector_8_c,
       subtraction_1_c__1er, subtraction_1_c__2er, subtraction_1_c__4er, subtraction_1_c__8er,
       subtraction_1_failsafe;

  _4bitadder _4bitadder_1 (
    .a__1er(in_11), .a__2er(in_12), .b__8er(selector_8_c), .b__4er(selector_7_c), .b__2er(selector_6_c),
    .b__1er(selector_5_c), .a__4er(in_13), .a__8er(in_14), .c__1er(_4bitadder_1_c__1er),
    .c__2er(_4bitadder_1_c__2er), .c__4er(_4bitadder_1_c__4er), .c__8er(_4bitadder_1_c__8er),
    .Failsafe(_4bitadder_1_failsafe));
  subtraction subtraction_1 (
    .b__1er(selector_5_c), .b__2er(selector_6_c), .b__4er(selector_7_c), .b__8er(selector_8_c),
    .a__8er(in_14), .a__4er(in_13), .a__2er(in_12), .a__1er(in_11), .Failsafe(subtraction_1_failsafe),
    .c__8er(subtraction_1_c__8er), .c__4er(subtraction_1_c__4er), .c__2er(subtraction_1_c__2er),
    .c__1er(subtraction_1_c__1er));
  selector selector_1 (.a(_4bitadder_1_c__1er), .b(subtraction_1_c__1er), .s(in_5), .c(out_1));
  selector selector_2 (.a(_4bitadder_1_c__2er), .b(subtraction_1_c__2er), .s(in_5), .c(out_2));
  selector selector_3 (.a(_4bitadder_1_c__4er), .b(subtraction_1_c__4er), .s(in_5), .c(out_3));
  selector selector_4 (.a(_4bitadder_1_c__8er), .b(subtraction_1_c__8er), .s(in_5), .c(out_4));
  or or_1 (out_15, subtraction_1_failsafe, _4bitadder_1_failsafe);
  selector selector_5 (.a(not_1_out), .b(in_6), .s(in_10), .c(selector_5_c));
  selector selector_6 (.a(1'b0), .b(in_7), .s(in_10), .c(selector_6_c));
  selector selector_7 (.a(1'b0), .b(in_8), .s(in_10), .c(selector_7_c));
  selector selector_8 (.a(1'b0), .b(in_9), .s(in_10), .c(selector_8_c));
  not not_1 (not_1_out, 1'b0);
endmodule
