// Digital circuit fulladder.dig as structural Verilog
module fulladder (
  input  a,
  input  b,
  input  c,
  output h,
  output l
);

  wire adder_1_h, adder_1_l, adder_2_h;

  adder adder_1 (.a(b), .b(c), .h(adder_1_h), .l(adder_1_l));
  adder adder_2 (.a(a), .b(adder_1_l), .h(adder_2_h), .l(l));
  adder adder_3 (.a(adder_2_h), .b(adder_1_h), .l(h));  // open: h
endmodule
