// Digital circuit logicunit.dig as structural Verilog
module logicunit (
  input  in_5,
  input  in_6,
  input  in_7,
  input  in_8,
  input  in_9,
  input  in_10,
  input  in_11,
  input  in_12,
  input  in_13,
  input  in_14,
  output out_1,
  output out_2,
  output out_3,
  output out_4
);

  wire and_1_out, nand_1_out, or_1_out, selector_1_c, selector_2_c, xor_1_out;

  selector selector_1 (.a(and_1_out), .b(or_1_out), .s(in_6), .c(selector_1_c));
  and and_1 (and_1_out, in_14, in_13, in_12, in_11, in_10, in_9, in_8, in_7);
  or or_1 (or_1_out, in_14, in_13, in_12, in_11, in_10, in_9, in_8, in_7);
  selector selector_2 (.a(nand_1_out), .b(xor_1_out), .s(in_6), .c(selector_2_c));
  xor xor_1 (xor_1_out, in_14, in_13, in_12, in_11, in_10, in_9, in_8, in_7);
  selector selector_3 (.a(selector_1_c), .b(selector_2_c), .s(in_5), .c(out_1));
  selector selector_4 (.a(1'b0), .b(1'b0), .s(in_5), .c(out_2));
  selector selector_5 (.a(1'b0), .b(1'b0), .s(in_5), .c(out_3));
  selector selector_6 (.a(1'b0), .b(1'b0), .s(in_5), .c(out_4));
  nand nand_1 (nand_1_out, in_14, in_13, in_12, in_11, in_10, in_9, in_8, in_7);
endmodule
