// Digital circuit selector.dig as structural Verilog
module selector (
  input  a,
  input  b,
  input  s,
  output c
);

  wire and_1_out, and_2_out, not_1_out;

  and and_1 (and_1_out, s, a);
  not not_1 (not_1_out, s);
  and and_2 (and_2_out, not_1_out, b);
  or or_1 (c, and_1_out, and_2_out);
endmodule
