// Digital circuit subtraction.dig as structural Verilog
module subtraction (
  input  b__1er,
  input  b__2er,
  input  b__4er,
  input  b__8er,
  input  a__8er,
  input  a__4er,
  input  a__2er,
  input  a__1er,
  output Failsafe,
  output c__8er,
  output c__4er,
  output c__2er,
  output c__1er
);

  wire _4bitadder_1_c__1er, _4bitadder_1_c__2er, _4bitadder_1_c__4er, _4bitadder_1_c__8er,
       _4bitadder_1_failsafe, _4bitadder_2_failsafe, not_1_out, not_2_out, not_3_out, not_4_out, not_5_out;

  not not_1 (not_1_out, b__8er);
  not not_2 (not_2_out, b__4er);
  not not_3 (not_3_out, b__2er);
  not not_4 (not_4_out, b__1er);
  not not_5 (not_5_out, 1'b0);
  _4bitadder _4bitadder_1 (
    .a__1er(not_4_out), .a__2er(not_3_out), .b__8er(1'b0), .b__4er(1'b0), .b__2er(1'b0), .b__1er(not_5_out),
    .a__4er(not_2_out), .a__8er(not_1_out), .c__1er(_4bitadder_1_c__1er), .c__2er(_4bitadder_1_c__2er),
    .c__4er(_4bitadder_1_c__4er), .c__8er(_4bitadder_1_c__8er), .Failsafe(_4bitadder_1_failsafe));
  _4bitadder _4bitadder_2 (
    .a__1er(a__1er), .a__2er(a__2er), .b__8er(_4bitadder_1_c__8er), .b__4er(_4bitadder_1_c__4er),
    .b__2er(_4bitadder_1_c__2er), .b__1er(_4bitadder_1_c__1er), .a__4er(a__4er), .a__8er(a__8er),
    .c__1er(c__1er), .c__2er(c__2er), .c__4er(c__4er), .c__8er(c__8er), .Failsafe(_4bitadder_2_failsafe));
  or or_1 (Failsafe, _4bitadder_1_failsafe, _4bitadder_2_failsafe);
endmodule
