// Digital circuit switch.dig as structural Verilog
module switch (
  input  in_1,
  input  in_2,
  output out_3,
  output out_4
);

  wire not_1_out;

  and and_1 (out_3, in_1, in_2);
  not not_1 (not_1_out, in_1);
  and and_2 (out_4, not_1_out, in_2);
endmodule
