// Digital circuit taktgeber.dig as structural Verilog
module taktgeber (
  input  clk,
  output out_2,
  output out_3
);

  _2BitZaehler _2bitzaehler_1 (.Clk(clk), .o1(out_2), .o2(out_3));
endmodule
